// Logisim project Bouncing Ball.circ as structural Verilog: 3 circuits, main circuit main
module main (
);

  wire clock_1_out, Reset_out;
  wire [2:0] horizontal_1_c, vertical_1_c;
  wire [7:0] decoder_1_out7, demultiplexer_1_out0, demultiplexer_1_out1, demultiplexer_1_out2,
       demultiplexer_1_out3, demultiplexer_1_out4, demultiplexer_1_out5, demultiplexer_1_out6,
       demultiplexer_1_out7;

  Button Reset (.out(Reset_out));
  Clock clock_1 (.out(clock_1_out));
  Horizontal horizontal_1 (
    .in_1(clock_1_out), .in_2(Reset_out), .A(horizontal_1_c[2]), .B(horizontal_1_c[1]), .C(horizontal_1_c[0]));
  Decoder #(.select(3)) decoder_1 (
    .out0(decoder_1_out7[7]), .out1(decoder_1_out7[6]), .out2(decoder_1_out7[5]), .out3(decoder_1_out7[4]),
    .out4(decoder_1_out7[3]), .out5(decoder_1_out7[2]), .out6(decoder_1_out7[1]), .out7(decoder_1_out7[0]),
    .sel(horizontal_1_c), .en(1'b1));
  Vertical vertical_1 (
    .in_1(clock_1_out), .in_2(Reset_out), .A(vertical_1_c[2]), .B(vertical_1_c[1]), .C(vertical_1_c[0]));
  Demultiplexer #(.select(3), .width(8)) demultiplexer_1 (
    .out0(demultiplexer_1_out0), .out1(demultiplexer_1_out1), .out2(demultiplexer_1_out2),
    .out3(demultiplexer_1_out3), .out4(demultiplexer_1_out4), .out5(demultiplexer_1_out5),
    .out6(demultiplexer_1_out6), .out7(demultiplexer_1_out7), .in(decoder_1_out7), .sel(vertical_1_c),
    .en(1'b1));
  DotMatrix #(.inputtype("row"), .matrixcols(8), .matrixrows(8)) dotmatrix_1 (
    .row0(demultiplexer_1_out0), .row1(demultiplexer_1_out1), .row2(demultiplexer_1_out2),
    .row3(demultiplexer_1_out3), .row4(demultiplexer_1_out4), .row5(demultiplexer_1_out5),
    .row6(demultiplexer_1_out6), .row7(demultiplexer_1_out7));
endmodule

module Vertical (
  input  in_1,
  input  in_2,
  output A,
  output B,
  output C
);

  wire and_1_out, and_2_out, and_3_out, and_4_out, and_5_out, and_6_out, j_k_ff_1_q, j_k_ff_1_qn,
       j_k_ff_2_qn, j_k_ff_3_qn, j_k_ff_4_qn, or_1_out, or_2_out;

  J_K_Flip_Flop j_k_ff_1 (
    .J(and_6_out), .clk(in_1), .K(and_1_out), .Q(j_k_ff_1_q), .Qn(j_k_ff_1_qn), .preset(1'b0), .en(1'b1),
    .reset(in_2));
  and and_1 (and_1_out, B, A);
  and and_2 (and_2_out, j_k_ff_1_q, C);
  and and_3 (and_3_out, and_2_out, B);
  and and_4 (and_4_out, and_5_out, j_k_ff_3_qn);
  and and_5 (and_5_out, j_k_ff_1_qn, j_k_ff_4_qn);
  and and_6 (and_6_out, j_k_ff_2_qn, j_k_ff_3_qn);
  J_K_Flip_Flop j_k_ff_2 (
    .J(and_3_out), .clk(in_1), .K(and_4_out), .Q(A), .Qn(j_k_ff_2_qn), .preset(1'b0), .en(1'b1), .reset(in_2));
  or or_1 (or_1_out, and_2_out, and_5_out);
  or or_2 (or_2_out, and_2_out, and_4_out);
  J_K_Flip_Flop j_k_ff_3 (
    .J(or_2_out), .clk(in_1), .K(or_1_out), .Q(B), .Qn(j_k_ff_3_qn), .preset(in_2), .en(1'b1), .reset(1'b0));
  J_K_Flip_Flop j_k_ff_4 (
    .J(1'b1), .clk(in_1), .K(1'b1), .Q(C), .Qn(j_k_ff_4_qn), .preset(1'b0), .en(1'b1), .reset(in_2));

  // Notes on the sheet:
  //   U
  //   A
  //   B
  //   C
endmodule

module Horizontal (
  input  in_1,
  input  in_2,
  output A,
  output B,
  output C
);

  wire and_1_out, and_2_out, and_3_out, and_4_out, and_5_out, and_6_out, j_k_ff_1_q, j_k_ff_1_qn,
       j_k_ff_2_qn, j_k_ff_3_qn, j_k_ff_4_qn, or_1_out, or_2_out;

  J_K_Flip_Flop j_k_ff_1 (
    .J(and_6_out), .clk(in_1), .K(and_1_out), .Q(j_k_ff_1_q), .Qn(j_k_ff_1_qn), .preset(in_2), .en(1'b1),
    .reset(1'b0));
  and and_1 (and_1_out, B, A);
  and and_2 (and_2_out, j_k_ff_1_q, C);
  and and_3 (and_3_out, and_2_out, B);
  and and_4 (and_4_out, and_5_out, j_k_ff_3_qn);
  and and_5 (and_5_out, j_k_ff_1_qn, j_k_ff_4_qn);
  and and_6 (and_6_out, j_k_ff_2_qn, j_k_ff_3_qn);
  J_K_Flip_Flop j_k_ff_2 (
    .J(and_3_out), .clk(in_1), .K(and_4_out), .Q(A), .Qn(j_k_ff_2_qn), .preset(1'b0), .en(1'b1), .reset(in_2));
  or or_1 (or_1_out, and_2_out, and_5_out);
  or or_2 (or_2_out, and_2_out, and_4_out);
  J_K_Flip_Flop j_k_ff_3 (
    .J(or_2_out), .clk(in_1), .K(or_1_out), .Q(B), .Qn(j_k_ff_3_qn), .preset(1'b0), .en(1'b1), .reset(in_2));
  J_K_Flip_Flop j_k_ff_4 (
    .J(1'b1), .clk(in_1), .K(1'b1), .Q(C), .Qn(j_k_ff_4_qn), .preset(in_2), .en(1'b1), .reset(1'b0));

  // Notes on the sheet:
  //   R
  //   A
  //   B
  //   C
endmodule
