// Logisim project 4bitMultiplier.circ as structural Verilog: 1 circuit, main circuit main
module main (
  input  [3:0] in_1,
  input  [3:0] in_2,
  output [7:0] out_3
);

  wire adder_1_cout, adder_2_cout, adder_4_cout, adder_6_cout, adder_8_cout, adder_9_cout;
  wire [3:0] adder_1_out, adder_2_out, adder_3_out, adder_4_out, adder_5_out, adder_6_out, adder_7_out,
       adder_8_out, adder_10_out, bit_extender_1_out, multiplexer_1_out, multiplexer_2_out,
       multiplexer_3_out, multiplexer_4_out, multiplexer_5_out, multiplexer_6_out, multiplexer_7_out;

  Adder #(.width(4)) adder_1 (.a(in_1), .b(in_1), .out(adder_1_out), .cout(adder_1_cout));  // open: cin
  Adder #(.width(4)) adder_2 (.a(adder_1_out), .b(adder_1_out), .out(adder_2_out), .cout(adder_2_cout));  // open: cin
  assign bit_extender_1_out = {{3{1'b0}}, adder_1_cout};  // Bit_Extender bit_extender_1
  Multiplexer #(.width(4), .disabled(0)) multiplexer_1 (
    .in0(in_1), .in1(in_1), .out(multiplexer_1_out), .sel(in_2[0]), .en(in_2[0]));
  Multiplexer #(.width(4), .disabled(0)) multiplexer_2 (
    .in0(adder_1_out), .in1(adder_1_out), .out(multiplexer_2_out), .sel(in_2[1]), .en(in_2[1]));
  Adder #(.width(4)) adder_3 (
    .a(bit_extender_1_out), .b(bit_extender_1_out), .out(adder_3_out), .cin(adder_2_cout));  // open: cout
  Multiplexer #(.width(4), .disabled(0)) multiplexer_3 (
    .in0(bit_extender_1_out), .in1(bit_extender_1_out), .out(multiplexer_3_out), .sel(in_2[1]), .en(in_2[1]));
  Multiplexer #(.width(4), .disabled(0)) multiplexer_4 (
    .in0(adder_2_out), .in1(adder_2_out), .out(multiplexer_4_out), .sel(in_2[2]), .en(in_2[2]));
  Adder #(.width(4)) adder_4 (.a(adder_2_out), .b(adder_2_out), .out(adder_4_out), .cout(adder_4_cout));  // open: cin
  Adder #(.width(4)) adder_5 (.a(adder_3_out), .b(adder_3_out), .out(adder_5_out), .cin(adder_4_cout));  // open: cout
  Adder #(.width(4)) adder_6 (
    .a(multiplexer_1_out), .b(multiplexer_2_out), .out(adder_6_out), .cout(adder_6_cout));  // open: cin
  Adder #(.width(4)) adder_7 (.a(4'b0000), .b(multiplexer_3_out), .out(adder_7_out), .cin(adder_6_cout));  // open: cout
  Multiplexer #(.width(4), .disabled(0)) multiplexer_5 (
    .in0(adder_3_out), .in1(adder_3_out), .out(multiplexer_5_out), .sel(in_2[2]), .en(in_2[2]));
  Multiplexer #(.width(4), .disabled(0)) multiplexer_6 (
    .in0(adder_4_out), .in1(adder_4_out), .out(multiplexer_6_out), .sel(in_2[3]), .en(in_2[3]));
  Multiplexer #(.width(4), .disabled(0)) multiplexer_7 (
    .in0(adder_5_out), .in1(adder_5_out), .out(multiplexer_7_out), .sel(in_2[3]), .en(in_2[3]));
  Adder #(.width(4)) adder_8 (
    .a(adder_6_out), .b(multiplexer_4_out), .out(adder_8_out), .cout(adder_8_cout));  // open: cin
  Adder #(.width(4)) adder_9 (
    .a(adder_8_out), .b(multiplexer_6_out), .out(out_3[3:0]), .cout(adder_9_cout));  // open: cin
  Adder #(.width(4)) adder_10 (
    .a(adder_7_out), .b(multiplexer_5_out), .out(adder_10_out), .cin(adder_8_cout));  // open: cout
  Adder #(.width(4)) adder_11 (
    .a(adder_10_out), .b(multiplexer_7_out), .out(out_3[7:4]), .cin(adder_9_cout));  // open: cout
  LED led_1 (.in(out_3[6]));
  LED led_2 (.in(out_3[5]));
  LED led_3 (.in(out_3[7]));
  LED led_4 (.in(out_3[3]));
  LED led_5 (.in(out_3[4]));
  LED led_6 (.in(out_3[2]));
  LED led_7 (.in(out_3[1]));
  LED led_8 (.in(out_3[0]));
endmodule
