// Logisim project HappySwitch.circ as structural Verilog: 1 circuit, main circuit main
module main (
);

  wire button_1_out, button_2_out, nand_1_out, nand_2_out, nand_3_out, nand_4_out;
  wire [3:0] multiplexer_1_out, multiplexer_2_out;

  Button button_1 (.out(button_1_out));
  Button button_2 (.out(button_2_out));
  nand nand_1 (nand_1_out, button_1_out, button_1_out);
  nand nand_2 (nand_2_out, button_2_out, button_2_out);
  nand nand_3 (nand_3_out, nand_1_out, nand_4_out);
  nand nand_4 (nand_4_out, nand_3_out, nand_2_out);
  DotMatrix #(.inputtype("row"), .matrixcols(4), .matrixrows(4)) dotmatrix_1 (
    .row0(4'b1001), .row1(4'b0000), .row2(multiplexer_1_out), .row3(multiplexer_2_out));
  Multiplexer #(.width(4), .disabled(0)) multiplexer_1 (
    .in0(4'b1111), .in1(4'b1001), .out(multiplexer_1_out), .sel(nand_3_out), .en(1'b1));
  Multiplexer #(.width(4), .disabled(0)) multiplexer_2 (
    .in0(4'b1001), .in1(4'b1111), .out(multiplexer_2_out), .sel(nand_3_out), .en(1'b1));
endmodule
