// Logisim project 2DPlayerMovement.circ as structural Verilog: 4 circuits, main circuit main
module main (
);

  wire a, and_1_out, and_2_out, and_3_out, and_4_out, and_5_out, and_6_out, and_7_out, and_8_out, and_9_out,
       button_2_out, button_3_out, button_4_out, button_out, clock_1_out, clock_2_out, clock_3_out,
       controlled_buffer_1_out, controlled_buffer_2_out, controlled_buffer_3_out, or_1_out, RESET_out;
  wire [2:1] obstacles_1_out_3, obstacles_1_out_4, obstacles_1_out_5, obstacles_1_out_6;
  wire [3:0] decoder_1_out0, decoder_1_out4, decoder_1_out8, decoder_1_out12, lrcounterjk_2_out_10;

  Clock #(.highDuration(3), .lowDuration(3)) clock_1 (.out(clock_1_out));
  Clock clock_2 (.out(clock_2_out));
  and and_1 (and_1_out, a, ~or_1_out);  // AND_Gate
  Button RESET (.out(RESET_out));
  Button button (.out(button_out));
  Clock clock_3 (.out(clock_3_out));
  assign controlled_buffer_1_out = and_1_out ? clock_3_out : 1'bz;  // Controlled_Buffer controlled_buffer_1
  assign controlled_buffer_2_out = and_1_out ? clock_1_out : 1'bz;  // Controlled_Buffer controlled_buffer_2
  assign controlled_buffer_3_out = and_1_out ? clock_2_out : 1'bz;  // Controlled_Buffer controlled_buffer_3
  Button button_2 (.out(button_2_out));
  Button button_3 (.out(button_3_out));
  Button button_4 (.out(button_4_out));
  Obstacles2 obstacles2_1 (
    .in_1(controlled_buffer_2_out), .in_2(RESET_out), .out_3(obstacles_1_out_3[2]),
    .out_4(obstacles_1_out_4[2]), .out_5(obstacles_1_out_5[2]), .out_6(obstacles_1_out_6[2]));
  Obstacles obstacles_1 (
    .in_1(controlled_buffer_3_out), .in_2(RESET_out), .out_3(obstacles_1_out_3[1]),
    .out_4(obstacles_1_out_4[1]), .out_5(obstacles_1_out_5[1]), .out_6(obstacles_1_out_6[1]));
  LRCounterJK lrcounterjk_1 (
    .L(button_out), .CLK(controlled_buffer_1_out), .R(button_4_out), .PRE1(RESET_out), .PRE2(1'b0),
    .CLR1(1'b0), .CLR2(RESET_out), .EN(1'b1), .out_9(lrcounterjk_2_out_10[3]),
    .out_10(lrcounterjk_2_out_10[2]));
  Decoder #(.select(4)) decoder_1 (
    .out0(decoder_1_out0[0]), .out1(decoder_1_out0[1]), .out2(decoder_1_out0[2]), .out3(decoder_1_out0[3]),
    .out4(decoder_1_out4[0]), .out5(decoder_1_out4[1]), .out6(decoder_1_out4[2]), .out7(decoder_1_out4[3]),
    .out8(decoder_1_out8[0]), .out9(decoder_1_out8[1]), .out10(decoder_1_out8[2]), .out11(decoder_1_out8[3]),
    .out12(decoder_1_out12[0]), .out13(decoder_1_out12[1]), .out14(decoder_1_out12[2]),
    .out15(decoder_1_out12[3]), .sel(lrcounterjk_2_out_10), .en(1'b1));
  LRCounterJK lrcounterjk_2 (
    .L(button_3_out), .CLK(controlled_buffer_1_out), .R(button_2_out), .PRE1(1'b0), .PRE2(1'b0),
    .CLR1(RESET_out), .CLR2(RESET_out), .EN(1'b1), .out_9(lrcounterjk_2_out_10[1]),
    .out_10(lrcounterjk_2_out_10[0]));
  or or_1 (or_1_out, decoder_1_out0[3], decoder_1_out4[3], decoder_1_out8[3], decoder_1_out12[3]);
  DotMatrix #(.matrixcols(4), .matrixrows(4)) dotmatrix_1 (
    .col0({1'b0, obstacles_1_out_3, 1'b0}), .col1({1'b0, obstacles_1_out_4, 1'b0}),
    .col2({1'b0, obstacles_1_out_5, 1'b0}), .col3({1'b0, obstacles_1_out_6, 1'b0}));
  DotMatrix #(.matrixcols(4), .matrixrows(4)) dotmatrix_2 (
    .col0(decoder_1_out0), .col1(decoder_1_out4), .col2(decoder_1_out8), .col3(decoder_1_out12));
  LED led_1 (.in(or_1_out));
  LED #(.active("false")) led_2 (.in(a));
  LED led_3 (.in(or_1_out));
  LED #(.active("false")) led_4 (.in(a));
  LED #(.active("false")) led_5 (.in(a));
  LED led_6 (.in(or_1_out));
  LED led_7 (.in(or_1_out));
  LED #(.active("false")) led_8 (.in(a));
  LED #(.active("false")) led_9 (.in(a));
  LED led_10 (.in(or_1_out));
  LED #(.active("false")) led_11 (.in(a));
  LED led_12 (.in(or_1_out));
  LED led_13 (.in(or_1_out));
  LED #(.active("false")) led_14 (.in(a));
  and and_2 (and_2_out, obstacles_1_out_3[1], decoder_1_out0[1]);
  and and_3 (and_3_out, obstacles_1_out_3[2], decoder_1_out0[2]);
  and and_4 (and_4_out, obstacles_1_out_4[1], decoder_1_out4[1]);
  and and_5 (and_5_out, obstacles_1_out_4[2], decoder_1_out4[2]);
  and and_6 (and_6_out, obstacles_1_out_5[1], decoder_1_out8[1]);
  and and_7 (and_7_out, obstacles_1_out_5[2], decoder_1_out8[2]);
  and and_8 (and_8_out, obstacles_1_out_6[1], decoder_1_out12[1]);
  and and_9 (and_9_out, obstacles_1_out_6[2], decoder_1_out12[2]);
  nor nor_1 (a, and_2_out, and_3_out, and_4_out, and_5_out, and_6_out, and_7_out, and_8_out, and_9_out);
endmodule

module LRCounterJK (
  input  L,
  input  CLK,
  input  R,
  input  PRE1,
  input  PRE2,
  input  CLR1,
  input  CLR2,
  input  EN,
  output out_9,
  output out_10
);

  wire A_prime_L_prime_R_out, ALR_prime_out, B_prime_LR_prime_out, BL_prime_R_out, j_k_ff_1_qn, j_k_ff_2_qn,
       L_prime_R_out, LR_prime_out, or_1_out, or_2_out;

  and LR_prime (LR_prime_out, L, ~R);  // AND_Gate
  and L_prime_R (L_prime_R_out, R, ~L);  // AND_Gate
  and A_prime_L_prime_R (A_prime_L_prime_R_out, j_k_ff_1_qn, L_prime_R_out);
  and B_prime_LR_prime (B_prime_LR_prime_out, j_k_ff_2_qn, LR_prime_out);
  and BL_prime_R (BL_prime_R_out, L_prime_R_out, out_10);
  and ALR_prime (ALR_prime_out, LR_prime_out, out_9);
  or or_1 (or_1_out, A_prime_L_prime_R_out, LR_prime_out);
  J_K_Flip_Flop j_k_ff_1 (
    .J(BL_prime_R_out), .clk(CLK), .K(B_prime_LR_prime_out), .Q(out_9), .Qn(j_k_ff_1_qn), .preset(PRE1),
    .en(EN), .reset(CLR1));
  or or_2 (or_2_out, L_prime_R_out, ALR_prime_out);
  J_K_Flip_Flop j_k_ff_2 (
    .J(or_2_out), .clk(CLK), .K(or_1_out), .Q(out_10), .Qn(j_k_ff_2_qn), .preset(PRE2), .en(EN), .reset(CLR2));
endmodule

module Obstacles (
  input  in_1,
  input  in_2,
  output out_3,
  output out_4,
  output out_5,
  output out_6
);

  wire d_ff_5_q;

  D_Flip_Flop d_ff_1 (.clk(in_1), .D(d_ff_5_q), .Q(out_3), .preset(1'b0), .en(1'b1), .reset(in_2));  // open: Qn
  D_Flip_Flop d_ff_2 (.clk(in_1), .D(out_3), .Q(out_4), .preset(1'b0), .en(1'b1), .reset(in_2));  // open: Qn
  D_Flip_Flop d_ff_3 (.clk(in_1), .D(out_4), .Q(out_5), .preset(1'b0), .en(1'b1), .reset(in_2));  // open: Qn
  D_Flip_Flop d_ff_4 (.clk(in_1), .D(out_5), .Q(out_6), .preset(1'b0), .en(1'b1), .reset(in_2));  // open: Qn
  D_Flip_Flop d_ff_5 (.clk(in_1), .D(out_6), .Q(d_ff_5_q), .preset(in_2), .en(1'b1), .reset(1'b0));  // open: Qn
endmodule

module Obstacles2 (
  input  in_1,
  input  in_2,
  output out_3,
  output out_4,
  output out_5,
  output out_6
);

  D_Flip_Flop d_ff_1 (.clk(in_1), .D(out_6), .Q(out_3), .preset(in_2), .en(1'b1), .reset(1'b0));  // open: Qn
  D_Flip_Flop d_ff_2 (.clk(in_1), .D(out_3), .Q(out_4), .preset(1'b0), .en(1'b1), .reset(in_2));  // open: Qn
  D_Flip_Flop d_ff_3 (.clk(in_1), .D(out_4), .Q(out_5), .preset(1'b0), .en(1'b1), .reset(in_2));  // open: Qn
  D_Flip_Flop d_ff_4 (.clk(in_1), .D(out_5), .Q(out_6), .preset(1'b0), .en(1'b1), .reset(in_2));  // open: Qn
endmodule
